// Digital circuit CPU.dig as structural Verilog
module CPU (
  input  clk
);

  wire add_2_s, calc_imm_1_p2, CI, wm, wreg;
  wire [1:0] B, \reg , undriven_2;
  wire [2:0] funct3, ula_op;
  wire [6:0] funct7, opcode;
  wire [23:0] rd, rs1, rs2;
  wire [31:0] BR_da, BR_db, imm, MD_d, multiplexer_1_out, multiplexer_2_out, multiplexer_3_out, pc_plus_4,
       PC_q, ula_out;
  wire [31:8] undriven;

  Multiplexer #(.Selector_Bits(2)) multiplexer_1 (
    .sel(undriven_2), .in_0(pc_plus_4[0]), .in_1(add_2_s), .in_2(ula_out[0]), .out(multiplexer_1_out[0]));  // open: in_3
  Register #(.Bits(32)) PC (.D(multiplexer_1_out), .C(clk), .en(1'b1), .Q(PC_q));
  Add #(.Bits(32)) add_1 (.a({undriven, 8'h4}), .b(PC_q), .s(pc_plus_4));  // open: c_i, c_o
  ROM #(.AddrBits(24), .Bits(32)) IM (
    .A(PC_q[23:0]), .sel(1'b1), .D({funct7, rs2[4:0], rs1[4:0], funct3, rd[4:0], opcode}));
  Add add_2 (.a(PC_q[0]), .b(imm[0]), .s(add_2_s));  // open: c_i, c_o
  // calc_imm calc_imm_1: pin names not known; wires that end beside it: {funct7, rs2[4:0], rs1[4:0], funct3, rd[4:0], opcode}, calc_imm_1_p2, imm
  // calc_type calc_type_1: pin names not known; wires that end beside it: opcode, funct3, funct7, calc_imm_1_p2
  CU cu_1 (
    .opc(opcode), .f3(funct3), .f7(funct7), .wreg(wreg), .ula_op(ula_op), .CI(CI), .resultSource(\reg ),
    .wm(wm), .PC_source(B));  // open: zero, Inv
  RegisterFile #(.AddrBits(24), .Bits(32)) BR (
    .Din(multiplexer_3_out), .we(wreg), .Rw(rd), .C(clk), .Ra(rs1), .Rb(rs2), .Da(BR_da), .Db(BR_db));
  Multiplexer #(.Bits(32)) multiplexer_2 (.sel(CI), .in_0(BR_db), .in_1(imm), .out(multiplexer_2_out));
  ULA ula_1 (.op1(BR_da), .op2(multiplexer_2_out), .Zero(ula_out[0]));  // open: controle, s
  RAMDualPort #(.AddrBits(24), .Bits(32)) MD (.Din(BR_db), .str(wm), .C(clk), .ld(1'b1), .D(MD_d));  // open: A
  Multiplexer #(.Selector_Bits(2), .Bits(32)) multiplexer_3 (
    .sel(\reg ), .in_1(pc_plus_4), .in_2(ula_out), .in_3(MD_d), .out(multiplexer_3_out));  // open: in_0
  // Pins of 1 and 32 bits meet at ula_out
  // Pins of 1 and 32 bits meet at multiplexer_1_out
  // Pins of 1 and 24 and 32 bits meet at PC_q
  // Pins of 8 and 32 bits meet at {undriven, 8'h4}
  // Pins of 1 and 32 bits meet at pc_plus_4
  // Pins of 5 and 24 bits meet at rd
  // Pins of 5 and 24 bits meet at rs1
  // Pins of 5 and 24 bits meet at rs2
  // Pins of 1 and 32 bits meet at imm
endmodule
