// Digital circuit ULA.dig as structural Verilog
module ULA (
  input  [31:0] op1,
  input  [31:0] op2,
  input  [2:0] controle,
  output [31:0] s
);

  wire comparator_1_eq, comparator_1_lt;
  wire [31:0] and_1_out, barrelshifter_1_out, bitextender_1_out, bitextender_2_out, bitextender_3_out,
       or_1_out, somador_1_s, subtrator_1_s, xor_1_out;

  somador somador_1 (.op1(op1), .op2(op2), .s(somador_1_s));
  subtrator subtrator_1 (.op1(op1), .op2(op2), .s(subtrator_1_s));
  assign xor_1_out = op1 ^ op2;  // XOr xor_1, 32 bits wide
  assign or_1_out = op1 | op2;  // Or or_1, 32 bits wide
  assign and_1_out = op1 & op2;  // And and_1, 32 bits wide
  Comparator #(.Signed("true"), .Bits(32)) comparator_1 (
    .a(op1), .b(op2), .eq(comparator_1_eq), .lt(comparator_1_lt));  // open: gt
  BarrelShifter #(.Bits(32), .barrelSigned("true")) barrelshifter_1 (.in(op1), .shift(op2), .out(barrelshifter_1_out));
  BitExtender #(.inputBits(1), .outputBits(32)) bitextender_1 (.in(comparator_1_eq), .out(bitextender_1_out));
  BitExtender #(.inputBits(1), .outputBits(32)) bitextender_2 (.in(comparator_1_lt), .out(bitextender_2_out));
  BitExtender #(.inputBits(1), .outputBits(32)) bitextender_3 (.in(barrelshifter_1_out[0]), .out(bitextender_3_out));
  Multiplexer #(.Selector_Bits(3), .Bits(32)) multiplexer_1 (
    .sel(controle), .in_0(somador_1_s), .in_1(subtrator_1_s), .in_2(xor_1_out), .in_3(or_1_out),
    .in_4(and_1_out), .in_5(bitextender_2_out), .in_6(bitextender_3_out), .in_7(bitextender_1_out), .out(s));
  // Pins of 1 and 32 bits meet at barrelshifter_1_out
endmodule
